# Fritzing sketch midterminternaltirgger (saved by Fritzing 0.9.3b)
breadboards: 1

parts:
  SparkFun_Haptic_Motor_Driver_-_DRV2605L1 = SparkFun Haptic Motor Driver - DRV2605L [part_number=ROB-14031]  # not connected
  U1 = Vibration Motor- ROB-08449 [package=vibe-motor-10mm]  # not connected
  Part1 = Arduino Uno (Rev3) - ICSP
  hc-sr1 = hc-sr04

nets:
  N1: Part1.D12/MISO, hc-sr1.Trig
  N2: Part1.D13/SCK, hc-sr1.Echo
  5V: Part1.5V, hc-sr1.VCC
  GND: Part1.GND, hc-sr1.GND

custom parts:
  SparkFun Haptic Motor Driver - DRV2605L: Description: Ready to add some good vibes to your project? Look no further than the SparkFun Haptic Motor Driver. This board breaks out Texas Instruments' DRV2605L Haptic Motor Driver, which adds meaningful feedback from your devices using the breakout and an Arduino-compatible device. The DRV2605L is capable of driving two different types of motors, ERM and LRA. It is important to know,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
